// Logisim project Computer.circ as structural Verilog: 1 circuit, main circuit main
module main (
);

  wire or_1_out;
  wire [7:0] A_q, adder_1_out, adder_2_out, B_q, BUS, controlled_buffer_1_out, controlled_buffer_4_out,
       controlled_buffer_6_out, controlled_buffer_8_out, controlled_buffer_9_out, controlled_buffer_11_out,
       controlled_buffer_12_out, controlled_buffer_13_out, IR_q, MAR_q, multiplexer_1_out, Output_q, PC_q,
       ram_1_data, subtractor_1_out;

  Adder adder_1 (.a(8'h1), .b(PC_q), .out(adder_1_out));  // open: cin, cout
  assign controlled_buffer_1_out = 1'b0 ? adder_1_out : 8'bz;  // Controlled_Buffer controlled_buffer_1
  Register PC (.D(controlled_buffer_1_out), .en(or_1_out), .Q(PC_q), .clk(1'b0));  // open: clr
  or or_1 (or_1_out, 1'b0, 1'b0);
  Register MAR (.D(controlled_buffer_4_out), .en(1'b0), .Q(MAR_q), .clk(1'b0));  // open: clr
  Register IR (.D(controlled_buffer_8_out), .en(1'b0), .Q(IR_q), .clk(1'b0));  // open: clr
  assign BUS = 1'b0 ? PC_q : 8'bz;  // Controlled_Buffer controlled_buffer_2
  assign controlled_buffer_1_out = 1'b0 ? BUS : 8'bz;  // Controlled_Buffer controlled_buffer_3
  assign controlled_buffer_4_out = 1'b0 ? controlled_buffer_11_out : 8'bz;  // Controlled_Buffer controlled_buffer_4
  RAM #(.bus("separate")) ram_1 (
    .addr(MAR_q), .din(controlled_buffer_6_out), .data(ram_1_data), .str(1'b0), .sel(1'b1), .clk(1'b0),
    .ld(1'b0));  // open: clr
  assign BUS = 1'b0 ? ram_1_data : 8'bz;  // Controlled_Buffer controlled_buffer_5
  assign controlled_buffer_6_out = 1'b0 ? BUS : 8'bz;  // Controlled_Buffer controlled_buffer_6
  assign BUS = 1'b0 ? IR_q : 8'bz;  // Controlled_Buffer controlled_buffer_7
  assign controlled_buffer_8_out = 1'b0 ? BUS : 8'bz;  // Controlled_Buffer controlled_buffer_8
  LED led_1 (.in(1'b0));
  DotMatrix #(.matrixcols(8), .matrixrows(1)) dotmatrix_1 (
    .col0(BUS[7]), .col1(BUS[6]), .col2(BUS[5]), .col3(BUS[4]), .col4(BUS[3]), .col5(BUS[2]), .col6(BUS[1]),
    .col7(BUS[0]));
  assign controlled_buffer_9_out = 1'b0 ? BUS : 8'bz;  // Controlled_Buffer controlled_buffer_9
  assign BUS = 1'b0 ? A_q : 8'bz;  // Controlled_Buffer controlled_buffer_10
  assign controlled_buffer_11_out = 1'b0 ? multiplexer_1_out : 8'bz;  // Controlled_Buffer controlled_buffer_11
  assign controlled_buffer_12_out = 1'b0 ? BUS : 8'bz;  // Controlled_Buffer controlled_buffer_12
  assign controlled_buffer_13_out = 1'b0 ? BUS : 8'bz;  // Controlled_Buffer controlled_buffer_13
  Register A (.D(controlled_buffer_9_out), .en(1'b0), .Q(A_q), .clk(1'b0));  // open: clr
  Register B (.D(controlled_buffer_12_out), .en(1'b0), .Q(B_q), .clk(1'b0));  // open: clr
  Register Output (.D(controlled_buffer_13_out), .en(1'b0), .Q(Output_q), .clk(1'b0));  // open: clr
  Hex_Digit_Display hex_digit_display_1 (.value(Output_q[7:4]));  // open: dp
  Hex_Digit_Display hex_digit_display_2 (.value(Output_q[3:0]));  // open: dp
  Adder adder_2 (.a(A_q), .b(B_q), .out(adder_2_out));  // open: cin, cout
  Multiplexer #(.width(8), .enable("false")) multiplexer_1 (
    .in0(adder_2_out), .in1(subtractor_1_out), .out(multiplexer_1_out), .sel(1'b0));
  Subtractor subtractor_1 (.a(A_q), .b(B_q), .out(subtractor_1_out));  // open: bin, bout

  // Notes on the sheet:
  //   RAM
  //   PC
  //   IR
  //   CONTROL
  //   B
  //   OR
  //   ACC
  //   ALU
endmodule
